# Fritzing sketch Plan (saved by Fritzing 0.9.9b)
circuit board: 8.46667cm x 5.64444cm
breadboards: 1

parts:
  Part1 = Arduino Nano (Rev3.0) (ICSP)
  Reciver = IC, SIP package, 6 pins [chip_label="Reciver 433"]
  Transmiter = IC, SIP package, 4 pins [chip_label=Transmiter]
  S1 = Round Pushbutton  # not connected
  LED1 = RGB LED - (4 legs) [package="5 mm [THT]"]

nets:
  N1: Part1.GND, Reciver.pin2, Transmiter.pin3
  N2: Part1.D2, Reciver.pin4
  N3: Part1.D10, Transmiter.pin1
  N4: Part1.3V3, Reciver.pin3, Transmiter.pin2
  N5: LED1.green_cathode, LED1.blue_cathode
